# Fritzing sketch isp (saved by Fritzing 0.9.2b)
circuit board: 3.19383cm x 3.0574cm
breadboards: 1

parts:
  Arduino_UNO = Arduino Uno (Rev3)
  Heartbeat = LED - 5mm [color="Green (555nm)" package="5 mm [THT]"]
  ERROR = LED - 5mm [color="Red (633nm)" package="5 mm [THT]"]
  Programming = LED - 5mm [color="Blue (470nm)" package="5 mm [THT]"]
  Arduino_DUE = Arduino Due (Rev2b)  # not connected
  R2 = Resistor [tolerance=±5% resistance=220 package=THT]
  R1 = Resistor [tolerance=±5% resistance=220 package=THT]
  R3 = Resistor [tolerance=±5% resistance=220 package=THT]

nets:
  N1: Arduino_UNO.D8, ERROR.anode
  N2: Arduino_UNO.D9_PWM, Heartbeat.anode
  N3: Arduino_UNO.GND, R2.Pin_0, R1.Pin_0, R3.Pin_0
  N4: Arduino_UNO.D7, Programming.anode
  N5: Heartbeat.cathode, R3.Pin_1
  N6: ERROR.cathode, R2.Pin_1
  N7: Programming.cathode, R1.Pin_1
