# Fritzing sketch BluetoothDemo (saved by Fritzing 0.9.1b)
circuit board: 4.62845cm x 5.28696cm
breadboards: 1

parts:
  Componente1 = Arduino Uno (Rev3)
  Componente2 = Bluetooth HC-05 Macho
  R1 = Resistor [tolerance=±5% resistance=1k package=THT]
  R2 = Resistor [tolerance=±5% resistance=2.2k package=THT]
  LED1 = LED - 3mm [color="Blue (430nm)" package="3 mm [THT]"]
  R3 = Resistor [tolerance=±5% resistance=470 package=THT]

nets:
  GND: Componente1.GND, Componente2.GND, R2.Pin_1, R3.Pin_1
  N1: Componente1.D0/RX, Componente2.TXD
  N2: Componente1.D1/TX, R1.Pin_0
  N3: Componente1.D2, LED1.anode
  5V: Componente1.5V, Componente2.VCC
  N4: Componente2.RXD, R1.Pin_1, R2.Pin_0
  N5: LED1.cathode, R3.Pin_0
