# Fritzing sketch DHT22 (saved by Fritzing 0.9.1b)
circuit board: 6.40645cm x 5.03297cm
breadboards: 1

parts:
  Sensor_Reading = DHT22 Humidity and Temperature Sensor
  Arduino_Nano = Arduino Nano (Rev3.0)
  LED1 = LED - 3mm [color="Blue (470nm)" package="3 mm [THT]"]
  LED2 = LED - 3mm [color="Green (555nm)" package="3 mm [THT]"]
  LED3 = LED - 3mm [color="White (4500K)" package="3 mm [THT]"]
  LED4 = LED - 3mm [color="Yellow (585nm)" package="3 mm [THT]"]
  LED5 = LED - 3mm [color="Orange (605nm)" package="3 mm [THT]"]
  LED6 = LED - 3mm [color="Red (633nm)" package="3 mm [THT]"]
  R1 = Resistor [tolerance=±5% resistance=220 package=THT]

nets:
  VDD: Sensor_Reading.VDD, Arduino_Nano.5V
  N1: Sensor_Reading.DATA, Arduino_Nano.D2
  GND: Sensor_Reading.GND, Arduino_Nano.GND, R1.Pin_1
  N2: Arduino_Nano.D3, LED6.anode
  N3: Arduino_Nano.D4, LED5.anode
  N4: Arduino_Nano.D5, LED4.anode
  N5: Arduino_Nano.D6, LED3.anode
  N6: Arduino_Nano.D7, LED2.anode
  N7: Arduino_Nano.D8, LED1.anode
  N8: LED1.cathode, LED2.cathode, LED3.cathode, LED4.cathode, LED5.cathode, LED6.cathode, R1.Pin_0

notes:
  Using DHT22 breakout with 5.1k pullup resistor

// code stored in the sketch: DHT22.ino
#include <DHT.h>

#define DHTPIN 2          // what pin we're connected to
#define DHTTYPE DHT22

// Initialize DHT sensor for normal 16mhz Arduino
DHT dht(DHTPIN, DHTTYPE);

//6 LEDs = 6 temp ranges
// pin 3 = 35+ C
// pin 4 = 30-35 C
// pin 5 = 25-30 C
// pin 6 = 20-25 C
// pin 7 = 15-20 C
// pin 8 = 15- C

void setup() {
  Serial.begin(9600); 
  Serial.println("Welcome to DHT22!");
  //LED
  pinMode(3, OUTPUT);
  pinMode(4, OUTPUT);
  pinMode(5, OUTPUT);
  pinMode(6, OUTPUT);
  pinMode(7, OUTPUT);
  pinMode(8, OUTPUT);
  pinMode(13, OUTPUT);
  dht.begin();
}

void loop() {
  // Wait a few seconds between measurements.
  delay(2000);
  
  digitalWrite(13, HIGH);   // turn the LED on when starts reading
  
  // Reading temperature or humidity takes about 250 milliseconds!
  // Sensor readings may also be up to 2 seconds 'old' (its a very slow sensor)
  float h = dht.readHumidity();
  // Read temperature as Celsius
  float t = dht.readTemperature();
  
  // Check if any reads failed and exit early (to try again).
  if (isnan(h) || isnan(t)) {
    Serial.println("Failed to read from DHT sensor!");
    return;
  }

  Serial.print("Humidity: "); 
  Serial.print(h);
  Serial.print(" %\t");
  Serial.print("Temperature: "); 
  Serial.print(t);
  Serial.println(" *C ");
  digitalWrite(13, LOW);   // turn the LED off when no reading.
  shutdownEverything();
  if (t<15) {
    digitalWrite(8, HIGH);
  }
  if (t>=15 && t<20) {
    digitalWrite(7, HIGH);
  }
  if (t>=20 && t<25) {
    digitalWrite(6, HIGH);
  }
  if (t>=25 && t<30) {
    digitalWrite(5, HIGH);
  }
  if (t>=30 && t<35) {
    digitalWrite(4, HIGH);
  }
  if (t<=35) {
    digitalWrite(3, HIGH);
  }
}

void shutdownEverything(){
  digitalWrite(3, LOW);
  digitalWrite(4, LOW);
  digitalWrite(5, LOW);
  digitalWrite(6, LOW);
  digitalWrite(7, LOW);
  digitalWrite(8, LOW);
}

// code stored in the sketch: LEDtester.ino
//test LEDs

void setup() {
	//LED
	pinMode(3, OUTPUT);
	pinMode(4, OUTPUT);
	pinMode(5, OUTPUT);
	pinMode(6, OUTPUT);
	pinMode(7, OUTPUT);
	pinMode(8, OUTPUT);
	//onboard LED
	pinMode(13, OUTPUT);
}

void loop() {
	//accende i LED in sequenza
	digitalWrite(3, HIGH);
	delay(200);
	digitalWrite(3, LOW);
	digitalWrite(4, HIGH);
	delay(200);
	digitalWrite(4, LOW);
	digitalWrite(5, HIGH);
	delay(200);
	digitalWrite(5, LOW);
	digitalWrite(6, HIGH);
	delay(200);
	digitalWrite(6, LOW);
	digitalWrite(7, HIGH);
	delay(200);
	digitalWrite(7, LOW);
	digitalWrite(8, HIGH);
	delay(200);
	digitalWrite(8, LOW);
	digitalWrite(13, HIGH);
	delay(200);
	digitalWrite(13, LOW);
}
