# Fritzing sketch NokiaLCD (saved by Fritzing 0.9.1b)
circuit board: 6.6717cm x 5.51539cm
breadboards: 2

parts:
  Componente1 = Arduino Nano (Rev3.0)
  Nokia_5110_LCD_Module1 = Nokia5110LCDModule
  IC1 = '4050 Hex Buffer

nets:
  GND: Componente1.GND, Nokia_5110_LCD_Module1.Grnd, IC1.VSS
  N1: Componente1.D3, IC1.A
  N2: Componente1.D4, IC1.B
  N3: Componente1.D5, IC1.C
  N4: Componente1.D6, IC1.E
  N5: Componente1.D7, IC1.F
  VCC: Componente1.3V3, Nokia_5110_LCD_Module1.Vcc, Nokia_5110_LCD_Module1.LED, IC1.VCC
  N6: Nokia_5110_LCD_Module1.SCE, IC1.H
  N7: Nokia_5110_LCD_Module1.RST, IC1.G
  N8: Nokia_5110_LCD_Module1.D/C, IC1.I
  N9: Nokia_5110_LCD_Module1.6_DN_(MOSI), IC1.L
  N10: Nokia_5110_LCD_Module1.SCLK, IC1.K

custom parts:
  : Nokia 5110 LCD with 8 pin. It's a 45mm*45mm module part. Description: The Nokia 5110 is a basic graphic LCD screen for lots of applications. It was originally intended for as a cell phone screen. This one is mounted on an easy to solder PCB. It uses the PCD8544 controller. The PCD8544 is a low power CMOS LCD controller/driver, designed to drive a graphic display of 48 rows and 84 columns. All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
