# Fritzing sketch eso8266demo (saved by Fritzing 0.9.1b)
circuit board: 8.46667cm x 5.64444cm
breadboards: 1

parts:
  WiFi = ESP8266 WiFi Module [part_number=ESP8266]
  Arduino_Mega = Arduino Mega 2560 (Rev3)

nets:
  N1: WiFi.RXD, Arduino_Mega.D18/TX1
  VCC: WiFi.VCC, WiFi.CH_PD, Arduino_Mega.3V3
  GND: WiFi.GND, Arduino_Mega.GND
  N2: WiFi.TXD, Arduino_Mega.D19/RX1

custom parts:
  ESP8266 WiFi Module: Generic WiFi Module based on the ESP8266 with onboard PCB antenna and UART communications
