# Fritzing sketch joyDemo (saved by Fritzing 0.9.1b)
circuit board: 5.35282cm x 5.43748cm

parts:
  Arduino = Arduino Uno (Rev3)
  Joypad = Thumb Joystick

nets:
  N1: Arduino.A0, Joypad.HORZ
  N2: Arduino.A1, Joypad.VERT
  GND: Arduino.GND, Joypad.GND
  N3: Arduino.D5_PWM, Joypad.SEL
  5V: Arduino.5V, Joypad.VCC
